# Fritzing sketch LCD-74HC595-3WIRE (saved by Fritzing 0.7.10b)
breadboards: 1

parts:
  U1 = 74HC595 SMD [package="SO16 [SMD]"]
  LCD1 = LCD screen
  J4 = Generic female header - 6 pins [package=THT]
  R2 = Resistor [tolerance=±5% resistance=220 package="0805 [SMD]"]
  C1 = Ceramic Capacitor [package=THT]
  C2 = Ceramic Capacitor [package=THT]
  POT1 = Breadboard Trimpot

nets:
  N1: U1.Q2, LCD1.RS
  N2: U1.Q3, LCD1.DB4
  N3: U1.Q4, LCD1.DB5
  N4: U1.Q5, LCD1.DB6
  N5: U1.Q6, LCD1.DB7
  GND: U1.GND, U1.OE, LCD1.VSS, LCD1.R/W, LCD1.LED-, J4.pin6, C1.pin_0, C2.pin_1, POT1.PIN1, POT1.PIN3
  VCC: U1.MR, U1.VCC, LCD1.VDD, J4.pin5, C1.pin_1, C2.pin_0
  N6: U1.SH_CP, J4.pin1
  N7: U1.ST_CP, LCD1.E, J4.pin3
  N8: U1.DS, J4.pin2
  N9: LCD1.V0, POT1.PIN2
  N10: LCD1.LED+, R2.Pin_0
  N11: J4.pin4, R2.Pin_1

notes:
  - Amarillo: Clock
  - Verde: Data
  - Blanco: Enabled
  - Marrón: Backlight
  R1: 220Ω
  C1: 0,1µF (#104)
  C2: 0,1µF (#104)
