# Fritzing sketch LCD-74HC595 (saved by Fritzing 0.7.10b)
breadboards: 1

parts:
  LCD1 = LCD screen
  U1 = 74HC595 [package="DIP16 [THT]"]
  D1 = Rectifier Diode [package=THT]
  C1 = Ceramic Capacitor [package=THT]
  C3 = Ceramic Capacitor [package=THT]
  C4 = Ceramic Capacitor [package=THT]
  R1 = 1k Ω Resistor [package=THT]
  R2 = Rotary Potentiometer (Large) [maximum_resistance=100kΩ package=THT]
  R3 = Resistor [tolerance=±5% resistance=220 package="0805 [SMD]"]
  J1 = Generic female header - 5 pins [package=THT]

nets:
  VSS: LCD1.VSS, LCD1.R/W, LCD1.LED-, U1.GND, C1.pin_0, C4.pin_0, R2.leg1
  N1: LCD1.VDD, C4.pin_1, R2.leg2
  N2: LCD1.V0, R2.wiper
  N3: LCD1.RS, U1.Q1
  N4: LCD1.E, R1.Pin_0
  N5: LCD1.DB4, U1.Q2
  N6: LCD1.DB5, U1.Q3
  N7: LCD1.DB6, U1.Q4
  N8: LCD1.DB7, U1.Q5
  N9: LCD1.LED+, R3.Pin_1
  N10: U1.Q6, D1.cathode, C1.pin_1
  N11: U1.MR, U1.VCC, C3.pin_1, J1.pin5
  N12: U1.SH_CP, U1.ST_CP, J1.pin2
  N13: U1.OE, C3.pin_0, J1.pin4
  N14: U1.DS, R1.Pin_1, J1.pin3
  N15: R3.Pin_0, J1.pin1

notes:
  Cable Naranja: BL
  Cable Morado: CLK
  Cable Amarillo: DAT
  Resistencias:
  1x220Ω
  1x1KΩ
  Diodos:
  1x1N4148
  Capacitores:
  2x0.1 uF
  1x0.01 uF
  Códigos de capacitores:
  0.1 uF = 100 nF = #104
  0.01 uF = 10 nF = #103
